# Fritzing sketch Cozinha (saved by Fritzing 0.9.3b)

parts:
  R1 = Resistor [tolerance=±5% resistance=10k package="0603 [SMD]"]
  S1 = Toggle Switch [package=THT]
  U2 = RELAY-SOLIDSTATE [package=relay-s108t02]
  R3 = Resistor [tolerance=±5% resistance=10k package="0603 [SMD]"]
  S2 = Toggle Switch [package=THT]
  U3 = RELAY-SOLIDSTATE [package=relay-s108t02]
  Power_plug1 = Power plug
  U1 = NodeMCU V1.0
  R8 = Resistor [tolerance=±5% resistance=6.8k package="0603 [SMD]"]
  R10 = Resistor [tolerance=±5% resistance=6.8k package="0603 [SMD]"]
  C1 = Electrolytic Capacitor [capacitance=1µF package="100 mil [THT, electrolytic]"]  # not connected
  C2 = Electrolytic Capacitor [capacitance=1µF package="100 mil [THT, electrolytic]"]
  C3 = Electrolytic Capacitor [capacitance=1µF package="100 mil [THT, electrolytic]"]  # not connected
  Q2 = Basic FET N-Channel [package="D2Pak [SMD]"]
  R11 = Resistor [tolerance=±5% resistance=10k package="0603 [SMD]"]

nets:
  N1: R1.Pin_0, R3.Pin_0, U1.GND, R10.Pin_1, C2.+, Q2.source, R11.Pin_1
  N2: R1.Pin_1, S1.L1, U1.D2
  N3: S1.COM, S1.L2, U1.3V3
  N4: U2.+, U1.D0, U1.D1, R10.Pin_0
  N5: U2.-, U3.-
  N6: R3.Pin_1, S2.L1
  N7: S2.COM, S2.L2
  N8: U3.+, U1.D5, R8.Pin_0
  GND: Power_plug1.GND, U1.Vin
  N9: U1.D3, Q2.Gate

notes:
  MQ2
  Válvula Solenoide

custom parts:
  NodeMCU V1.0: ESP8266 based NodeMCU
