# Fritzing sketch LEDIR (saved by Fritzing 0.9.3b)
breadboards: 1

parts:
  U1 = NodeMCU V1.0  # not connected
  Q1 = NPN-Transistor [package="TO92 [THT]"]
  D1 = LTE-302 [package=lte-302]

nets:
  N1: Q1.E, D1.A

custom parts:
  NodeMCU V1.0: ESP8266 based NodeMCU
